# Fritzing sketch LightPaintbrush (saved by Fritzing 0.9.1b)
breadboards: 1

parts:
  TRINKET1 = Trinket 5V
  POT1 = Breadboard Trimpot
  S1 = Momentary Switch [package=tactile-pth]
  S2 = Momentary Switch [package=tactile-pth]
  S3 = Momentary Switch [package=tactile-pth]
  R1 = Resistor [tolerance=±5% resistance=10k package=THT]
  R2 = Resistor [tolerance=±5% resistance=10k package=THT]
  R3 = Resistor [tolerance=±5% resistance=10k package=THT]
  RGB_SMD_LED1 = SMD RGB LED (WS2812) [package=5050]
  BATT1 = 3xAAA Switchable Battery Pack w/Bare Wire
  R4 = Resistor [tolerance=±5% resistance=100 package=THT]

nets:
  N1: TRINKET1.no_name_yet#2, POT1.PIN3, S1.4, S2.4, S3.4, RGB_SMD_LED1.VSS, BATT1.NEG
  N2: TRINKET1.no_name_yet#3, S2.2, R1.Pin_0
  N3: TRINKET1.no_name_yet#4, POT1.PIN2
  VCC: TRINKET1.no_name_yet#6, POT1.PIN1, R1.Pin_1, R2.Pin_1, R3.Pin_1, RGB_SMD_LED1.VCC, RGB_SMD_LED1.VDD, BATT1.POS
  N4: TRINKET1.no_name_yet#7, S1.3
  N5: TRINKET1.no_name_yet#8, R4.Pin_0
  N6: TRINKET1.no_name_yet#9, S3.3
  N7: S1.2, R2.Pin_0
  N8: S3.2, R3.Pin_0
  N9: RGB_SMD_LED1.DIn, R4.Pin_1

custom parts:
  Trinket 5V: Adafruit Trinket 5V
  3xAAA Switchable Battery Pack w/Bare Wire: 3xAAA Switchable Battery Pack w/Bare Wire Connectors
